// Logisim project Datapath.circ as structural Verilog
module main (
  input  in_1,
  output [15:0] out_2,
  output [15:0] out_3,
  output [15:0] out_4,
  output [3:0] OP,
  output [3:0] RS,
  output [3:0] RT,
  output [3:0] RD_IM,
  output [15:0] out_9
);

  wire and_1_out, button_1_out, clock_1_out, control_unit_1_binv, control_unit_1_cin, control_unit_1_im,
       control_unit_1_jump, control_unit_1_memread, control_unit_1_memtoreg, control_unit_1_memwrite,
       control_unit_1_nop, control_unit_1_ramen, control_unit_1_regdest, control_unit_1_writeen,
       n16_bit_alu_2_0_1_zero, not_1_out;
  wire [2:0] control_unit_1_alu_op;
  wire [3:0] multiplexer_1_out;
  wire [15:0] adder_1_out, bit_extender_1_out, multiplexer_3_out, multiplexer_4_out, ram_1_data, register_1_q;

  Clock clock_1 (.out(clock_1_out));
  Register #(.width(16)) register_1 (
    .D(multiplexer_3_out), .en(not_1_out), .Q(register_1_q), .clk(clock_1_out));  // open: clr
  Adder #(.width(16)) adder_1 (.a(16'h1), .b(register_1_q), .out(adder_1_out), .cin(in_1));  // open: cout
  ROM #(.addrWidth(16), .dataWidth(16)) rom_1 (.addr(register_1_q), .data({OP, RS, RT, RD_IM}));  // open: sel
  Control_Unit control_unit_1 (
    .in_1(OP), .WriteEn(control_unit_1_writeen), .Cin(control_unit_1_cin), .Binv(control_unit_1_binv),
    .RamEn(control_unit_1_ramen), .MemWrite(control_unit_1_memwrite), .MemRead(control_unit_1_memread),
    .RegDest(control_unit_1_regdest), .IM(control_unit_1_im), .ALU_OP(control_unit_1_alu_op),
    .MemToReg(control_unit_1_memtoreg), .Jump(control_unit_1_jump), .nop(control_unit_1_nop));
  not not_1 (not_1_out, control_unit_1_nop);
  Multiplexer #(.width(4), .enable("false")) multiplexer_1 (
    .in0(RD_IM), .in1(RT), .out(multiplexer_1_out), .sel(control_unit_1_regdest));
  Register_File register_file_1 (
    .Write_Data(multiplexer_4_out), .Write_Register(multiplexer_1_out), .Read_Data_1(out_3),
    .Read_Data_2(out_2), .Write_enable(control_unit_1_writeen), .Clk(clock_1_out), .Clr(button_1_out),
    .Read_Register_1(RS), .Read_Register_2(RT));
  assign bit_extender_1_out = {{12{1'b0}}, RD_IM};  // Bit_Extender bit_extender_1
  Multiplexer #(.width(16), .enable("false")) multiplexer_2 (
    .in0(out_2), .in1(bit_extender_1_out), .out(out_4), .sel(control_unit_1_im));
  Multiplexer #(.width(16), .enable("false")) multiplexer_3 (
    .in0(adder_1_out), .in1(bit_extender_1_out), .out(multiplexer_3_out), .sel(and_1_out));
  and and_1 (and_1_out, control_unit_1_jump, n16_bit_alu_2_0_1_zero);
  _16_bit_ALU_2_0 u_16_bit_alu_2_0_1 (
    .Cin(control_unit_1_cin), .ALU_OP(control_unit_1_alu_op), .Binv(control_unit_1_binv), .A(out_3),
    .B(out_4), .out_6(out_9), .Zero(n16_bit_alu_2_0_1_zero));  // open: Cout
  Button button_1 (.out(button_1_out));
  Multiplexer #(.width(16), .enable("false")) multiplexer_4 (
    .in0(out_9), .in1(ram_1_data), .out(multiplexer_4_out), .sel(control_unit_1_memtoreg));
  RAM #(.addrWidth(16), .dataWidth(16), .bus("separate")) ram_1 (
    .addr(out_9), .din(out_2), .data(ram_1_data), .str(control_unit_1_memwrite), .sel(control_unit_1_ramen),
    .clk(clock_1_out), .ld(control_unit_1_memread), .clr(button_1_out));
endmodule

module Register_File (
  input  [15:0] Write_Data,
  input  [3:0] Read_Register_1,
  input  [3:0] Write_Register,
  input  [3:0] Read_Register_2,
  input  Write_enable,
  input  Clk,
  input  Clr,
  output [15:0] Read_Data_1,
  output [15:0] Read_Data_2
);

  wire and_1_out, and_2_out, and_3_out, and_4_out, and_5_out, and_6_out, and_7_out, and_8_out, and_9_out,
       and_10_out, and_11_out, and_12_out, and_13_out, and_14_out, and_15_out, and_16_out, decoder_1_out0,
       decoder_1_out1, decoder_1_out2, decoder_1_out3, decoder_1_out4, decoder_1_out5, decoder_1_out6,
       decoder_1_out7, decoder_1_out8, decoder_1_out9, decoder_1_out10, decoder_1_out11, decoder_1_out12,
       decoder_1_out13, decoder_1_out14, decoder_1_out15;
  wire [15:0] _0_q, _1_q, _2_q, _3_q, _4_q, _5_q, _6_q, _7_q, _8_q, _9_q, _10_q, _11_q, _12_q, _13_q, _14_q,
       _15_q;

  Decoder #(.select(4)) decoder_1 (
    .out0(decoder_1_out0), .out1(decoder_1_out1), .out2(decoder_1_out2), .out3(decoder_1_out3),
    .out4(decoder_1_out4), .out5(decoder_1_out5), .out6(decoder_1_out6), .out7(decoder_1_out7),
    .out8(decoder_1_out8), .out9(decoder_1_out9), .out10(decoder_1_out10), .out11(decoder_1_out11),
    .out12(decoder_1_out12), .out13(decoder_1_out13), .out14(decoder_1_out14), .out15(decoder_1_out15),
    .sel(Write_Register));  // open: en
  and and_1 (and_1_out, Write_enable, decoder_1_out0);
  and and_2 (and_2_out, Write_enable, decoder_1_out1);
  and and_3 (and_3_out, Write_enable, decoder_1_out2);
  and and_4 (and_4_out, Write_enable, decoder_1_out3);
  and and_5 (and_5_out, Write_enable, decoder_1_out4);
  and and_6 (and_6_out, Write_enable, decoder_1_out5);
  and and_7 (and_7_out, Write_enable, decoder_1_out6);
  and and_8 (and_8_out, Write_enable, decoder_1_out7);
  and and_9 (and_9_out, Write_enable, decoder_1_out8);
  and and_10 (and_10_out, Write_enable, decoder_1_out9);
  and and_11 (and_11_out, Write_enable, decoder_1_out10);
  and and_12 (and_12_out, Write_enable, decoder_1_out11);
  and and_13 (and_13_out, Write_enable, decoder_1_out12);
  and and_14 (and_14_out, Write_enable, decoder_1_out13);
  and and_15 (and_15_out, Write_enable, decoder_1_out14);
  and and_16 (and_16_out, Write_enable, decoder_1_out15);
  Register #(.width(16)) _0 (.en(and_1_out), .Q(_0_q), .clk(Clk), .clr(Clr));  // open: D
  Register #(.width(16)) _1 (.D(Write_Data), .en(and_2_out), .Q(_1_q), .clk(Clk), .clr(Clr));
  Register #(.width(16)) _2 (.D(Write_Data), .en(and_3_out), .Q(_2_q), .clk(Clk), .clr(Clr));
  Register #(.width(16)) _3 (.D(Write_Data), .en(and_4_out), .Q(_3_q), .clk(Clk), .clr(Clr));
  Register #(.width(16)) _4 (.D(Write_Data), .en(and_5_out), .Q(_4_q), .clk(Clk), .clr(Clr));
  Register #(.width(16)) _5 (.D(Write_Data), .en(and_6_out), .Q(_5_q), .clk(Clk), .clr(Clr));
  Register #(.width(16)) _6 (.D(Write_Data), .en(and_7_out), .Q(_6_q), .clk(Clk), .clr(Clr));
  Register #(.width(16)) _7 (.D(Write_Data), .en(and_8_out), .Q(_7_q), .clk(Clk), .clr(Clr));
  Register #(.width(16)) _8 (.D(Write_Data), .en(and_9_out), .Q(_8_q), .clk(Clk), .clr(Clr));
  Register #(.width(16)) _9 (.D(Write_Data), .en(and_10_out), .Q(_9_q), .clk(Clk), .clr(Clr));
  Register #(.width(16)) _10 (.D(Write_Data), .en(and_11_out), .Q(_10_q), .clk(Clk), .clr(Clr));
  Register #(.width(16)) _11 (.D(Write_Data), .en(and_12_out), .Q(_11_q), .clk(Clk), .clr(Clr));
  Register #(.width(16)) _12 (.D(Write_Data), .en(and_13_out), .Q(_12_q), .clk(Clk), .clr(Clr));
  Register #(.width(16)) _13 (.D(Write_Data), .en(and_14_out), .Q(_13_q), .clk(Clk), .clr(Clr));
  Register #(.width(16)) _14 (.D(Write_Data), .en(and_15_out), .Q(_14_q), .clk(Clk), .clr(Clr));
  Register #(.width(16)) _15 (.D(Write_Data), .en(and_16_out), .Q(_15_q), .clk(Clk), .clr(Clr));
  Multiplexer #(.select(4), .width(16)) multiplexer_1 (
    .in0(_0_q), .in1(_1_q), .in2(_2_q), .in3(_3_q), .in4(_4_q), .in5(_5_q), .in6(_6_q), .in7(_7_q),
    .in8(_8_q), .in9(_9_q), .in10(_10_q), .in11(_11_q), .in12(_12_q), .in13(_13_q), .in14(_14_q),
    .in15(_15_q), .out(Read_Data_1), .sel(Read_Register_1));  // open: en
  Multiplexer #(.select(4), .width(16)) multiplexer_2 (
    .in0(_0_q), .in1(_1_q), .in2(_2_q), .in3(_3_q), .in4(_4_q), .in5(_5_q), .in6(_6_q), .in7(_7_q),
    .in8(_8_q), .in9(_9_q), .in10(_10_q), .in11(_11_q), .in12(_12_q), .in13(_13_q), .in14(_14_q),
    .in15(_15_q), .out(Read_Data_2), .sel(Read_Register_2));  // open: en
endmodule

module _1_bit_ALU (
  input  A,
  input  B,
  input  Cin,
  input  [1:0] in_4,
  input  Binv,
  output out_6,
  output Cout
);

  wire adder_1_out, and_1_out, multiplexer_1_out, not_1_out, or_1_out;

  not not_1 (not_1_out, B);
  Multiplexer multiplexer_1 (.in0(B), .in1(not_1_out), .out(multiplexer_1_out), .sel(Binv));  // open: en
  and and_1 (and_1_out, A, B);
  or or_1 (or_1_out, A, B);
  Adder #(.width(1)) adder_1 (.a(A), .b(multiplexer_1_out), .out(adder_1_out), .cin(Cin), .cout(Cout));
  Multiplexer #(.select(2)) multiplexer_2 (
    .in0(and_1_out), .in1(or_1_out), .in2(adder_1_out), .out(out_6), .sel(in_4));  // open: in3, en
endmodule

module _16_bit_ALU (
  input  [15:0] A,
  input  [15:0] B,
  input  [1:0] Operation,
  input  Cin,
  input  Binv,
  output [15:0] out_6,
  output Zero_Detection,
  output Overflow,
  output Cout
);

  wire n1_bit_alu_1_cout, n1_bit_alu_2_cout, n1_bit_alu_3_cout, n1_bit_alu_4_cout, n1_bit_alu_5_cout,
       n1_bit_alu_6_cout, n1_bit_alu_7_cout, n1_bit_alu_8_cout, n1_bit_alu_9_cout, n1_bit_alu_10_cout,
       n1_bit_alu_11_cout, n1_bit_alu_12_cout, n1_bit_alu_13_cout, n1_bit_alu_14_cout, n1_bit_alu_15_cout;

  _1_bit_ALU u_1_bit_alu_1 (
    .in_4(Operation), .out_6(out_6[0]), .Cout(n1_bit_alu_1_cout), .A(A[0]), .B(B[0]), .Cin(Cin), .Binv(Binv));
  _1_bit_ALU u_1_bit_alu_2 (
    .in_4(Operation), .out_6(out_6[1]), .Cout(n1_bit_alu_2_cout), .A(A[1]), .B(B[1]),
    .Cin(n1_bit_alu_1_cout), .Binv(Binv));
  _1_bit_ALU u_1_bit_alu_3 (
    .in_4(Operation), .out_6(out_6[2]), .Cout(n1_bit_alu_3_cout), .A(A[2]), .B(B[2]),
    .Cin(n1_bit_alu_2_cout), .Binv(Binv));
  _1_bit_ALU u_1_bit_alu_4 (
    .in_4(Operation), .out_6(out_6[3]), .Cout(n1_bit_alu_4_cout), .A(A[3]), .B(B[3]),
    .Cin(n1_bit_alu_3_cout), .Binv(Binv));
  _1_bit_ALU u_1_bit_alu_5 (
    .in_4(Operation), .out_6(out_6[4]), .Cout(n1_bit_alu_5_cout), .A(A[4]), .B(B[4]),
    .Cin(n1_bit_alu_4_cout), .Binv(Binv));
  _1_bit_ALU u_1_bit_alu_6 (
    .in_4(Operation), .out_6(out_6[5]), .Cout(n1_bit_alu_6_cout), .A(A[5]), .B(B[5]),
    .Cin(n1_bit_alu_5_cout), .Binv(Binv));
  _1_bit_ALU u_1_bit_alu_7 (
    .in_4(Operation), .out_6(out_6[6]), .Cout(n1_bit_alu_7_cout), .A(A[6]), .B(B[6]),
    .Cin(n1_bit_alu_6_cout), .Binv(Binv));
  _1_bit_ALU u_1_bit_alu_8 (
    .in_4(Operation), .out_6(out_6[7]), .Cout(n1_bit_alu_8_cout), .A(A[7]), .B(B[7]),
    .Cin(n1_bit_alu_7_cout), .Binv(Binv));
  _1_bit_ALU u_1_bit_alu_9 (
    .in_4(Operation), .out_6(out_6[8]), .Cout(n1_bit_alu_9_cout), .A(A[8]), .B(B[8]),
    .Cin(n1_bit_alu_8_cout), .Binv(Binv));
  _1_bit_ALU u_1_bit_alu_10 (
    .in_4(Operation), .out_6(out_6[9]), .Cout(n1_bit_alu_10_cout), .A(A[9]), .B(B[9]),
    .Cin(n1_bit_alu_9_cout), .Binv(Binv));
  _1_bit_ALU u_1_bit_alu_11 (
    .in_4(Operation), .out_6(out_6[10]), .Cout(n1_bit_alu_11_cout), .A(A[10]), .B(B[10]),
    .Cin(n1_bit_alu_10_cout), .Binv(Binv));
  _1_bit_ALU u_1_bit_alu_12 (
    .in_4(Operation), .out_6(out_6[11]), .Cout(n1_bit_alu_12_cout), .A(A[11]), .B(B[11]),
    .Cin(n1_bit_alu_11_cout), .Binv(Binv));
  _1_bit_ALU u_1_bit_alu_13 (
    .in_4(Operation), .out_6(out_6[12]), .Cout(n1_bit_alu_13_cout), .A(A[12]), .B(B[12]),
    .Cin(n1_bit_alu_12_cout), .Binv(Binv));
  _1_bit_ALU u_1_bit_alu_14 (
    .in_4(Operation), .out_6(out_6[13]), .Cout(n1_bit_alu_14_cout), .A(A[13]), .B(B[13]),
    .Cin(n1_bit_alu_13_cout), .Binv(Binv));
  _1_bit_ALU u_1_bit_alu_15 (
    .in_4(Operation), .out_6(out_6[14]), .Cout(n1_bit_alu_15_cout), .A(A[14]), .B(B[14]),
    .Cin(n1_bit_alu_14_cout), .Binv(Binv));
  _1_bit_ALU u_1_bit_alu_16 (
    .in_4(Operation), .out_6(out_6[15]), .Cout(Cout), .A(A[15]), .B(B[15]), .Cin(n1_bit_alu_15_cout),
    .Binv(Binv));
  xor xor_1 (Overflow, n1_bit_alu_15_cout, Cout);
  nor nor_1 (Zero_Detection, out_6[0], out_6[1], out_6[2], out_6[3], out_6[4], out_6[5], out_6[6], out_6[7], out_6[8], out_6[9], out_6[10], out_6[11], out_6[12], out_6[13], out_6[14], out_6[15]);
endmodule

module _16_bit_ALU_2_0 (
  input  [15:0] A,
  input  [15:0] B,
  input  Cin,
  input  [2:0] ALU_OP,
  input  Binv,
  output [15:0] out_6,
  output Zero,
  output Cout
);

  wire comparator_1_lt;
  wire [3:0] bit_extender_1_out;
  wire [15:0] adder_1_out, and_1_out, bit_extender_2_out, multiplexer_1_out, not_1_out, not_2_out, or_1_out,
       shifter_1_out;

  assign not_1_out = ~B;  // NOT_Gate not_1, 16 bits wide
  assign and_1_out = A & B;  // AND_Gate and_1, 16 bits wide
  assign or_1_out = A | B;  // OR_Gate or_1, 16 bits wide
  assign not_2_out = ~A;  // NOT_Gate not_2, 16 bits wide
  Multiplexer #(.width(16)) multiplexer_1 (.in0(B), .in1(not_1_out), .out(multiplexer_1_out), .sel(Binv));  // open: en
  Bit_Extender #(.in_width(16), .out_width(4)) bit_extender_1 (.in(B), .out(bit_extender_1_out));
  Comparator #(.width(16)) comparator_1 (.a(A), .b(B), .lt(comparator_1_lt));  // open: gt, eq
  Shifter #(.width(16)) shifter_1 (.in(A), .\dist (bit_extender_1_out), .out(shifter_1_out));
  assign bit_extender_2_out = {{15{1'b0}}, comparator_1_lt};  // Bit_Extender bit_extender_2
  Adder #(.width(16)) adder_1 (.a(A), .b(multiplexer_1_out), .out(adder_1_out), .cin(Cin), .cout(Cout));
  Multiplexer #(.select(3), .width(16)) multiplexer_2 (
    .in0(and_1_out), .in1(or_1_out), .in2(not_2_out), .in3(adder_1_out), .in4(shifter_1_out),
    .in5(bit_extender_2_out), .out(out_6), .sel(ALU_OP));  // open: in6, in7, en
  nor nor_1 (Zero, out_6[0], out_6[1], out_6[2], out_6[3], out_6[4], out_6[5], out_6[6], out_6[7], out_6[8], out_6[9], out_6[10], out_6[11], out_6[12], out_6[13], out_6[14], out_6[15]);
endmodule

module Control_Unit (
  input  [3:0] in_1,
  output WriteEn,
  output nop,
  output Cin,
  output Binv,
  output RamEn,
  output MemWrite,
  output MemRead,
  output MemToReg,
  output RegDest,
  output IM,
  output [2:0] ALU_OP,
  output Jump
);

  wire decoder_1_out1, decoder_1_out2, decoder_1_out4, decoder_1_out5, decoder_1_out6, decoder_1_out7,
       decoder_1_out8, decoder_1_out9;

  Decoder #(.select(4), .enable("false")) decoder_1 (
    .out0(nop), .out1(decoder_1_out1), .out2(decoder_1_out2), .out3(MemWrite), .out4(decoder_1_out4),
    .out5(decoder_1_out5), .out6(decoder_1_out6), .out7(decoder_1_out7), .out8(decoder_1_out8),
    .out9(decoder_1_out9), .out10(MemRead), .sel(in_1));  // open: out11, out12, out13, out14, out15
  or or_1 (ALU_OP[0], decoder_1_out2, MemWrite, decoder_1_out5, decoder_1_out7, decoder_1_out8, decoder_1_out9, MemRead);
  or or_2 (ALU_OP[1], decoder_1_out2, MemWrite, decoder_1_out5, decoder_1_out8, decoder_1_out9, MemRead);
  or or_3 (ALU_OP[2], decoder_1_out1, decoder_1_out7);
  or or_4 (RamEn, MemWrite, MemRead);
  or or_5 (IM, MemWrite, decoder_1_out1, decoder_1_out6, MemRead, decoder_1_out9);
  or or_6 (WriteEn, decoder_1_out1, decoder_1_out2, decoder_1_out4, decoder_1_out7, decoder_1_out8, decoder_1_out9, MemRead);
  or or_7 (Cin, decoder_1_out2, decoder_1_out5);
  or or_8 (Binv, decoder_1_out2, decoder_1_out5);
  or or_9 (RegDest, decoder_1_out9, decoder_1_out1, MemRead);
  or or_10 (Jump, decoder_1_out5, decoder_1_out6);

  assign MemToReg = MemRead;
endmodule
